# Fritzing sketch joystick-rp2040 (saved by Fritzing 1.0.1rc)
breadboards: 1

parts:
  Mod1 = Raspberry Pi Pico  # not connected
  Componente1 = Thumb Joystick
  Componente2 = Thumb Joystick
  Componente3 = NRF24L01+ Breakout Board
  LED1 = smd LED [color="Red (633nm)" package="1206 [SMD]"]
  LED2 = smd LED [color="Green (560nm)" package="1206 [SMD]"]
  R2 = Resistor [tolerance=±5% resistance=80 package="0603 [SMD]"]
  LED3 = smd LED [color="White (6500K)" package="1206 [SMD]"]
  R3 = Resistor [tolerance=±5% resistance=80 package="0603 [SMD]"]
  R4 = Resistor [tolerance=±5% resistance=80 package="0603 [SMD]"]
  S1 = Pushbutton [package=THT]
  S2 = Pushbutton [package=THT]

nets:
  GND: Componente1.GND, Componente2.GND
  VCC: Componente1.VCC, Componente2.VCC
  N1: Componente3.GND, LED1.cathode, LED2.cathode
  N2: LED1.anode, R3.Pin_0
  N3: LED2.anode, R2.Pin_0
  N4: LED3.cathode, S1.leg0, S2.leg0
  N5: LED3.anode, R4.Pin_0

custom parts:
  Raspberry Pi Pico: Raspberry Pi Pico. Based around the RP2040 microcontroller the Pico is a low cost microcontroller device bringing Raspberry Pi quality, cost, and easy of use to the microcontroller space. Jan 2021, Split part in to two versions: tht (this one) and SMD. This one will drill holes for a .1 in header in pcb to allow plugging in the module as well as providing pads to solder the module to the top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
