# Fritzing sketch joystick-simple (saved by Fritzing 1.0.1rc)

parts:
  Componente1 = Thumb Joystick
  Componente2 = Arduino Uno (Rev3) - ICSP

nets:
  GND: Componente1.GND, Componente2.GND
  N1: Componente1.SEL, Componente2.D6_PWM
  N2: Componente1.HORZ, Componente2.A1
  N3: Componente1.VERT, Componente2.A0
  VCC: Componente1.VCC, Componente2.5V
